# Fritzing sketch Trimmer-PICO-PWM (saved by Fritzing 0.9.9b)
breadboards: 1

parts:
  Mod1 = Raspberry Pi Pico
  R2 = Trimmer Potentiometer [maximum_resistance=10kΩ package=THT]
  P1 = Multimeter straight black probe  # not connected
  P2 = Multimeter straight red probe

nets:
  N1: Mod1.pin_3, Mod1.pin_8, Mod1.pin_13, Mod1.pin_18, Mod1.pin_23, Mod1.pin_28, Mod1.pin_33, Mod1.pin_38, Mod1.pin_42, R2.leg2
  N2: Mod1.pin_36, R2.leg1
  N3: R2.wiper, P2.Probe_tip

custom parts:
  Raspberry Pi Pico: Raspberry Pi Pico. Based around the RP2040 microcontroller the Pico is a low cost microcontroller device bringing Raspberry Pi quality, cost, and easy of use to the microcontroller space. Jan 2021, Split part in to two versions: tht (this one) and SMD. This one will drill holes for a .1 in header in pcb to allow plugging in the module as well as providing pads to solder the module to the top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
