# Fritzing sketch E-Stop and Limit Switch (saved by Fritzing 0.9.9b)
breadboards: 1

parts:
  Mod1 = Raspberry Pi Pico
  LED1 = smd LED [color="Red (633nm)" package="0805 [SMD]"]
  LED2 = smd LED [color="Red (633nm)" package="0805 [SMD]"]
  D2F1 = D2F-FL Omron Snap Action Limit Switch with Level
  S1 = Round Pushbutton
  R1 = Resistor [tolerance=±5% resistance=220 package="0805 [SMD]"]
  R2 = Resistor [tolerance=±5% resistance=220 package="0805 [SMD]"]

nets:
  N1: Mod1.pin_3, Mod1.pin_8, Mod1.pin_13, Mod1.pin_18, Mod1.pin_23, Mod1.pin_28, Mod1.pin_33, Mod1.pin_38, LED1.cathode, LED2.cathode, D2F1.NO, S1.leg1
  N2: Mod1.pin_19, D2F1.COM
  N3: Mod1.pin_20, R2.Pin_0
  N4: Mod1.pin_21, R1.Pin_0
  N5: Mod1.pin_22, S1.leg0
  N6: LED1.anode, R2.Pin_1
  N7: LED2.anode, R1.Pin_1

notes:
  LIMIT SWITCH
  EMERGENCY STOP

custom parts:
  Raspberry Pi Pico: Raspberry Pi Pico. Based around the RP2040 microcontroller the Pico is a low cost microcontroller device bringing Raspberry Pi quality, cost, and easy of use to the microcontroller space. Jan 2021, Split part in to two versions: tht (this one) and SMD. This one will drill holes for a .1 in header in pcb to allow plugging in the module as well as providing pads to solder the module to the top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
  D2F-FL Omron Snap Action Limit Switch with Level: Snap action switch with stainless steel lever.
