# Fritzing sketch A3144-WO PICO (saved by Fritzing 0.9.10b)
breadboards: 1

parts:
  U1 = A3144 Hall Effect Sensor. [package="UA [THT]"]
  LED1 = smd LED [color="Red (633nm)" package="0603 [SMD]"]
  R1 = Resistor [tolerance=±5% resistance=220 package="0805 [SMD]"]

nets:
  N1: U1.+Vsupply, R1.Pin_1
  N2: U1.Out, LED1.cathode
  N3: LED1.anode, R1.Pin_0

notes:
  NOTE- Shape of 3144 is backwards!!!
  5 volts
  0 volts

custom parts:
  A3144 Hall Effect Sensor.: Allegro A3144 hall effect switch for high temperature operation.
