# Fritzing sketch PICO-MCP23017 (saved by Fritzing 0.9.9b)
breadboards: 3

parts:
  Mod1 = Raspberry Pi Pico
  IC1 = MCP23017 I2C I/O Expander
  SW1 = DIP Switch 8 Position [package=dipswitch-08]
  D1 = LED_BARGRAPH_10 [package=led_bargaph_10]
  R1 = Resistor [tolerance=±5% resistance=330 package="0603 [SMD]"]
  R2 = Resistor [tolerance=±5% resistance=330 package="0603 [SMD]"]
  R3 = Resistor [tolerance=±5% resistance=330 package="0603 [SMD]"]
  R4 = Resistor [tolerance=±5% resistance=330 package="0603 [SMD]"]
  R5 = Resistor [tolerance=±5% resistance=330 package="0603 [SMD]"]
  R6 = Resistor [tolerance=±5% resistance=330 package="0603 [SMD]"]
  R7 = Resistor [tolerance=±5% resistance=330 package="0603 [SMD]"]
  R8 = Resistor [tolerance=±5% resistance=330 package="0603 [SMD]"]

nets:
  N1: Mod1.pin_3, Mod1.pin_8, Mod1.pin_13, Mod1.pin_18, Mod1.pin_23, Mod1.pin_28, Mod1.pin_33, Mod1.pin_38, IC1.VSS, IC1.A0, IC1.A1, IC1.A2, SW1.1, SW1.2, SW1.3, SW1.4, SW1.5, SW1.7, SW1.8, R1.Pin_0, R2.Pin_0, R3.Pin_0, R4.Pin_0, R5.Pin_0, R7.Pin_0, R8.Pin_0
  N2: Mod1.pin_26, IC1.SDA
  N3: Mod1.pin_27, IC1.SCL
  N4: Mod1.pin_36, IC1.VDD
  N5: IC1.GPB0, SW1.16
  N6: IC1.GPB1, SW1.15
  N7: IC1.GPB2, SW1.14
  N8: IC1.GPB3, SW1.13
  N9: IC1.GPB4, SW1.12
  N10: IC1.GPB5, SW1.11
  N11: IC1.GPB6, SW1.10
  N12: IC1.GPB7, SW1.9
  N13: IC1.GPA0, D1.H_A
  N14: IC1.GPA1, D1.G_A
  N15: IC1.GPA2, D1.F_A
  N16: IC1.GPA3, D1.E_A
  N17: IC1.GPA4, D1.D_A
  N18: IC1.GPA5, D1.C_A
  N19: IC1.GPA6, D1.B_A
  N20: IC1.GPA7, D1.A_A
  N21: D1.H_C, R8.Pin_1
  N22: D1.G_C, R7.Pin_1
  N23: D1.F_C, R6.Pin_1
  N24: D1.E_C, R5.Pin_1
  N25: D1.D_C, R4.Pin_1
  N26: D1.C_C, R3.Pin_1
  N27: D1.B_C, R2.Pin_1
  N28: D1.A_C, R1.Pin_1

custom parts:
  Raspberry Pi Pico: Raspberry Pi Pico. Based around the RP2040 microcontroller the Pico is a low cost microcontroller device bringing Raspberry Pi quality, cost, and easy of use to the microcontroller space. Jan 2021, Split part in to two versions: tht (this one) and SMD. This one will drill holes for a .1 in header in pcb to allow plugging in the module as well as providing pads to solder the module to the top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
  MCP23017 I2C I/O Expander: The MCP23017 uses two i2c pins (these can be shared with other i2c devices), and in exchange gives you 16 general purpose pins. You can set each of 16 pins to be input, output, input with a pullup or open drain. There's even the ability to get an interrupt via an external pin when any of the inputs change so you don't have to keep polling the chip.
