# Fritzing sketch PICO to Analog Keypad (saved by Fritzing 0.9.9b)
breadboards: 1

parts:
  Matrix_keypad1 = KEYPAD 4x4  # not connected
  Mod1 = Raspberry Pi Pico
  J1 = Dagu DGServo 9g header connector (female) [package=THT]

nets:
  N1: Mod1.pin_3, Mod1.pin_8, Mod1.pin_13, Mod1.pin_18, Mod1.pin_23, Mod1.pin_28, Mod1.pin_33, Mod1.pin_38, J1.Vcc
  N2: Mod1.pin_31, J1.gnd
  N3: Mod1.pin_36, J1.pulse

notes:
  OUT
  GND
  VCC

custom parts:
  KEYPAD 4x4: Matrix keypad 16 buttons, 4 rows x 4 columns
  Raspberry Pi Pico: Raspberry Pi Pico. Based around the RP2040 microcontroller the Pico is a low cost microcontroller device bringing Raspberry Pi quality, cost, and easy of use to the microcontroller space. Jan 2021, Split part in to two versions: tht (this one) and SMD. This one will drill holes for a .1 in header in pcb to allow plugging in the module as well as providing pads to solder the module to the top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
