# Fritzing sketch The Clapper (saved by Fritzing 0.9.10b)
breadboards: 1

parts:
  FC-1 = Sound Sensor
  Mod1 = Raspberry Pi Pico
  LED1 = smd LED [color="Red (633nm)" package="1206 [SMD]"]
  R1 = Resistor [tolerance=±5% power=0.25 resistance=220 package=THT]

nets:
  N1: FC-1.VCC, Mod1.pin_36
  N2: FC-1.GND, Mod1.pin_3, Mod1.pin_8, Mod1.pin_13, Mod1.pin_18, Mod1.pin_23, Mod1.pin_28, Mod1.pin_33, Mod1.pin_38, LED1.cathode
  N3: FC-1.OUT, Mod1.pin_20
  N4: Mod1.pin_19, R1.Pin_1
  N5: LED1.anode, R1.Pin_0

custom parts:
  Raspberry Pi Pico: Raspberry Pi Pico. Based around the RP2040 microcontroller the Pico is a low cost microcontroller device bringing Raspberry Pi quality, cost, and easy of use to the microcontroller space. Jan 2021, Split part in to two versions: tht (this one) and SMD. This one will drill holes for a .1 in header in pcb to allow plugging in the module as well as providing pads to solder the module to the top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
