# Fritzing sketch Basic Connections (saved by Fritzing 0.9.9b)

parts:
  RELAY1 = CAR RELAY [part_number=NVF4-2 package=THT]
  Mod1 = Raspberry Pi Pico
  VCC1 = Battery
  U1 = DIODE-ZENER [package=diode-zener]  # not connected
  Q1 = NPN-Transistor [package="TO92 [THT]"]  # not connected
  U2 = Optocoupler [package=THT]  # not connected
  M1 = DC Motor
  VCC2 = Battery block 9V

nets:
  N1: RELAY1.85, M1.pin_1
  N2: RELAY1.86, VCC2.+
  N3: Mod1.pin_23, Mod1.pin_38, VCC1.-
  N4: Mod1.pin_40, VCC1.+
  N5: M1.pin_2, VCC2.-

notes:
  RELAY
  DIODE
  Opto
  Coupler
  Transistor

custom parts:
  Raspberry Pi Pico: Raspberry Pi Pico. Based around the RP2040 microcontroller the Pico is a low cost microcontroller device bringing Raspberry Pi quality, cost, and easy of use to the microcontroller space. Jan 2021, Split part in to two versions: tht (this one) and SMD. This one will drill holes for a .1 in header in pcb to allow plugging in the module as well as providing pads to solder the module to the top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
