# Fritzing sketch Relay-ULN2803 (saved by Fritzing 0.9.10b)

parts:
  RELAY1 = CAR RELAY [part_number=NVF4-2 package=THT]
  Mod1 = Raspberry Pi Pico
  M1 = DC Motor [voltage_(max)=6V voltage_(min)=3V]
  VCC2 = Battery block 9V
  IC1 = ULN2803A [package=THT]

nets:
  N1: RELAY1.85, M1.pin_1
  N2: RELAY1.86, VCC2.+
  N3: Mod1.pin_21, IC1.In_1
  N4: Mod1.pin_23, Mod1.pin_42, IC1.0V
  N5: Mod1.pin_40, IC1.COM_-_Common
  N6: M1.pin_2, VCC2.-

notes:
  RELAY

custom parts:
  Raspberry Pi Pico: Raspberry Pi Pico. Based around the RP2040 microcontroller the Pico is a low cost microcontroller device bringing Raspberry Pi quality, cost, and easy of use to the microcontroller space. Jan 2021, Split part in to two versions: tht (this one) and SMD. This one will drill holes for a .1 in header in pcb to allow plugging in the module as well as providing pads to solder the module to the top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
