# Fritzing sketch RelayModule1 ULN2803 (saved by Fritzing 0.9.10b)

parts:
  Mod1 = Raspberry Pi Pico
  M1 = DC Motor [voltage_(max)=6V voltage_(min)=3V]
  VCC2 = Battery block 9V
  IC1 = ULN2803A [package=THT]
  WeMos_D1_Mini_Relay_Shield_V1 = WeMos D1 Mini Relay Shield V2
  R1 = Resistor [tolerance=±5% power=0.25 resistance=2.2k package=THT]

nets:
  N1: Mod1.pin_21, IC1.In_1
  N2: Mod1.pin_23, Mod1.pin_42, IC1.0V, WeMos_D1_Mini_Relay_Shield_V1.D4
  N3: Mod1.pin_40, IC1.COM_-_Common
  N4: M1.pin_2, VCC2.-
  N5: IC1.Out_1, WeMos_D1_Mini_Relay_Shield_V1.D1, R1.Pin_1

notes:
  GND
  VCC
  CH1
  2.2kR

custom parts:
  Raspberry Pi Pico: Raspberry Pi Pico. Based around the RP2040 microcontroller the Pico is a low cost microcontroller device bringing Raspberry Pi quality, cost, and easy of use to the microcontroller space. Jan 2021, Split part in to two versions: tht (this one) and SMD. This one will drill holes for a .1 in header in pcb to allow plugging in the module as well as providing pads to solder the module to the top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
