# Fritzing sketch Matrix Keypad Digital (saved by Fritzing 0.9.9b)
breadboards: 1

parts:
  Keypad4x2 = Keypad Membran 4x4
  Mod1 = Raspberry Pi Pico

nets:
  N1: Keypad4x2.Pin2, Mod1.pin_19
  N2: Keypad4x2.Pin3, Mod1.pin_17
  N3: Keypad4x2.Pin4, Mod1.pin_16
  N4: Keypad4x2.Pin5, Mod1.pin_15
  N5: Keypad4x2.Pin6, Mod1.pin_14
  N6: Keypad4x2.Pin7, Mod1.pin_12
  N7: Keypad4x2.Pin8, Mod1.pin_11
  N8: Mod1.pin_3, Mod1.pin_8, Mod1.pin_13, Mod1.pin_18, Mod1.pin_23, Mod1.pin_28, Mod1.pin_33, Mod1.pin_38

custom parts:
  Keypad Membran 4x4: Membrane Keypad 4x4 Matrix
  Raspberry Pi Pico: Raspberry Pi Pico. Based around the RP2040 microcontroller the Pico is a low cost microcontroller device bringing Raspberry Pi quality, cost, and easy of use to the microcontroller space. Jan 2021, Split part in to two versions: tht (this one) and SMD. This one will drill holes for a .1 in header in pcb to allow plugging in the module as well as providing pads to solder the module to the top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
