# Fritzing sketch HC-SR04 (saved by Fritzing 0.9.9b)
breadboards: 1

parts:
  HC-SR04_Sensor_1 = HC-SR04 Ultrasonic Distance Sensor
  Mod1 = Raspberry Pi Pico
  Part1 = Logic Level Converter

nets:
  N1: HC-SR04_Sensor_1.VCC, Mod1.pin_40, Part1.HV
  N2: HC-SR04_Sensor_1.TRIG, Part1.TX_HV
  N3: HC-SR04_Sensor_1.ECHO, Part1.RX_HV
  GND: HC-SR04_Sensor_1.GND, Mod1.pin_3, Mod1.pin_8, Mod1.pin_13, Mod1.pin_18, Mod1.pin_23, Mod1.pin_28, Mod1.pin_33, Mod1.pin_38, Mod1.pin_42, Part1.GND
  N4: Mod1.pin_19, Part1.RX_LV
  N5: Mod1.pin_20, Part1.TX_LV
  N6: Mod1.pin_36, Part1.LV

notes:
  LEVEL SHIFTER

custom parts:
  Raspberry Pi Pico: Raspberry Pi Pico. Based around the RP2040 microcontroller the Pico is a low cost microcontroller device bringing Raspberry Pi quality, cost, and easy of use to the microcontroller space. Jan 2021, Split part in to two versions: tht (this one) and SMD. This one will drill holes for a .1 in header in pcb to allow plugging in the module as well as providing pads to solder the module to the top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
