# Fritzing sketch HIH-4030 PICO Schematic (saved by Fritzing 0.9.10b)
breadboards: 2

parts:
  Mod1 = Raspberry Pi Pico
  U1 = HIH-4030 [package=hih-4030]
  Mod2 = Raspberry Pi Pico
  U2 = HIH-4030 [package=hih-4030]
  Part1 = Logic Level Converter

nets:
  N1: Mod1.pin_3, Mod1.pin_8, Mod1.pin_13, Mod1.pin_18, Mod1.pin_23, Mod1.pin_28, Mod1.pin_33, Mod1.pin_38, U1.GND
  N2: Mod1.pin_34, U1.OUT
  N3: Mod1.pin_40, U1.VCC
  GND: Mod2.pin_3, Mod2.pin_8, Mod2.pin_13, Mod2.pin_18, Mod2.pin_23, Mod2.pin_28, Mod2.pin_33, Mod2.pin_38, U2.GND, Part1.GND
  N4: Mod2.pin_34, Part1.TX2_LV
  N5: Mod2.pin_36, Part1.LV
  N6: Mod2.pin_40, U2.VCC

notes:
  BAD EXAMPLE - ANALOG VOLTAGE WILL BE ABOVE 3.3V!!!
  USE A LEVEL SHIFTER TO REDUCE ANALOG VOLTAGE

custom parts:
  Raspberry Pi Pico: Raspberry Pi Pico. Based around the RP2040 microcontroller the Pico is a low cost microcontroller device bringing Raspberry Pi quality, cost, and easy of use to the microcontroller space. Jan 2021, Split part in to two versions: tht (this one) and SMD. This one will drill holes for a .1 in header in pcb to allow plugging in the module as well as providing pads to solder the module to the top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
