# Fritzing sketch IR Beam Break (saved by Fritzing 0.9.9b)
breadboards: 1

parts:
  Mod1 = Raspberry Pi Pico
  M1 = IR break beam 3mm tx [package=THT]
  M2 = IR break beam 3mm rx [package=THT]

nets:
  N1: Mod1.pin_3, Mod1.pin_8, Mod1.pin_13, Mod1.pin_18, Mod1.pin_23, Mod1.pin_28, Mod1.pin_33, Mod1.pin_38, M1.pin2, M2.pin3
  N2: Mod1.pin_21, M2.pin2
  N3: Mod1.pin_40, M1.pin1, M2.pin1

notes:
  IR Diode
  IR Detector
  5V

custom parts:
  Raspberry Pi Pico: Raspberry Pi Pico. Based around the RP2040 microcontroller the Pico is a low cost microcontroller device bringing Raspberry Pi quality, cost, and easy of use to the microcontroller space. Jan 2021, Split part in to two versions: tht (this one) and SMD. This one will drill holes for a .1 in header in pcb to allow plugging in the module as well as providing pads to solder the module to the top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
  IR break beam 3mm tx: Infrared break beam Sensor tx module.
  IR break beam 3mm rx: Infrared break beam Sensor rx module.
