# Fritzing sketch PICO W Many Relays (saved by Fritzing 0.9.10b)
breadboards: 3

parts:
  Mod1 = Raspberry Pi Pico
  IC2 = ULN2803A [package=THT]
  OMRON1 = OMRON PCB Power Relay – G5LE [part_number="G5LE-1\r\n" package=THT]
  OMRON2 = OMRON PCB Power Relay – G5LE [part_number="G5LE-1\r\n" package=THT]
  VCC1 = 4 x AAA Battery Mount
  OMRON3 = OMRON PCB Power Relay – G5LE [part_number="G5LE-1\r\n" package=THT]
  OMRON4 = OMRON PCB Power Relay – G5LE [part_number="G5LE-1\r\n" package=THT]
  OMRON5 = OMRON PCB Power Relay – G5LE [part_number="G5LE-1\r\n" package=THT]
  OMRON6 = OMRON PCB Power Relay – G5LE [part_number="G5LE-1\r\n" package=THT]
  LED1 = Super Flux LED blue [color=Blue current=0.030A]
  R1 = Resistor [tolerance=±5% power=0.25 resistance=50 package=THT]
  LED2 = Super Flux LED blue [color=Blue current=0.030A]
  LED3 = Super Flux LED blue [color=Blue current=0.030A]
  LED4 = Super Flux LED blue [color=Blue current=0.030A]
  R2 = Resistor [tolerance=±5% power=0.25 resistance=50 package=THT]
  R3 = Resistor [tolerance=±5% power=0.25 resistance=50 package=THT]
  R4 = Resistor [tolerance=±5% power=0.25 resistance=50 package=THT]
  LED5 = Super Flux LED blue [color=Blue current=0.030A]
  R5 = Resistor [tolerance=±5% power=0.25 resistance=50 package=THT]
  R6 = Resistor [tolerance=±5% power=0.25 resistance=50 package=THT]
  LED6 = Super Flux LED blue [color=Blue current=0.030A]

nets:
  N1: Mod1.pin_3, Mod1.pin_8, Mod1.pin_13, Mod1.pin_18, Mod1.pin_23, Mod1.pin_28, Mod1.pin_33, Mod1.pin_38, IC2.0V, VCC1.-
  N2: Mod1.pin_16, IC2.In_4
  N3: Mod1.pin_17, IC2.In_3
  N4: Mod1.pin_19, IC2.In_2
  N5: Mod1.pin_20, IC2.In_1
  N6: Mod1.pin_26, IC2.In_5
  N7: Mod1.pin_34, IC2.In_6
  N8: IC2.COM_-_Common, OMRON1.COIL2, OMRON2.COIL2, VCC1.+, OMRON3.COIL2, OMRON4.COIL2, OMRON4.B, OMRON5.COIL2, OMRON6.COIL2, OMRON6.B
  N9: IC2.Out_6, OMRON6.COIL1
  N10: IC2.Out_5, OMRON5.COIL1
  N11: IC2.Out_4, OMRON4.COIL1
  N12: IC2.Out_3, OMRON3.COIL1
  N13: IC2.Out_2, OMRON2.COIL1
  N14: IC2.Out_1, OMRON1.COIL1
  N15: LED1.cathode, LED2.cathode, LED3.cathode, LED4.cathode, LED5.cathode, LED6.cathode
  N16: LED1.anode, R1.Pin_0
  N17: LED2.anode, R2.Pin_0
  N18: LED3.anode, R3.Pin_0
  N19: LED4.anode, R4.Pin_0
  N20: LED5.anode, R5.Pin_0
  N21: R6.Pin_0, LED6.anode

notes:
  5V External PS
  Notice PICO power
  is not used on loads.
  Multilpe Relays Driving High Loads
  It is powered by USB
  PICO is Buffered with ULN2803

custom parts:
  Raspberry Pi Pico: Raspberry Pi Pico. Based around the RP2040 microcontroller the Pico is a low cost microcontroller device bringing Raspberry Pi quality, cost, and easy of use to the microcontroller space. Jan 2021, Split part in to two versions: tht (this one) and SMD. This one will drill holes for a .1 in header in pcb to allow plugging in the module as well as providing pads to solder the module to the top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
