# Fritzing sketch HollowClock (saved by Fritzing 0.9.10b)

parts:
  Mod1 = Raspberry Pi Pico
  S1 = SWITCH-MOMENTARY-2 [package=tactile-pth-12mm]  # not connected
  S2 = SWITCH-MOMENTARY-2 [package=tactile-pth-12mm]  # not connected
  S3 = SWITCH-MOMENTARY-2 [package=tactile-pth-12mm]  # not connected
  JP4 = Header 6 [package=molex-1x6-ra]  # not connected
  JP5 = Header 6 [package=molex-1x6-ra]
  JP6 = Header 4 [package=molex-1x4_lock]
  M1 = Stepper Motor - Unipolar
  J1 = Camdenboss CTB0158-2 [part_number=CTB0158-2 package=THT]
  J2 = Camdenboss CTB0158-4 [part_number=CTB0158-4 package=THT]

nets:
  N1: Mod1.pin_14, J2.pin4
  N2: Mod1.pin_15, J2.pin3
  N3: Mod1.pin_16, J2.pin2
  N4: Mod1.pin_17, J2.pin1
  N5: Mod1.pin_23, Mod1.pin_38, Mod1.pin_42, JP6.1, J1.pin2
  N6: Mod1.pin_24, JP6.2
  N7: Mod1.pin_25, JP6.3
  N8: Mod1.pin_26, JP6.4
  N9: Mod1.pin_40, J1.pin1
  N10: JP5.6, M1.A

notes:
  RED
  YELLOW
  GREEN
  Stick On Membrane Key Pad
  Stepper Driver
  Stepper Motor
  Power is supplied to PICO with
  Transformer & Micro USB Cable

custom parts:
  Raspberry Pi Pico: Raspberry Pi Pico. Based around the RP2040 microcontroller the Pico is a low cost microcontroller device bringing Raspberry Pi quality, cost, and easy of use to the microcontroller space. Jan 2021, Split part in to two versions: tht (this one) and SMD. This one will drill holes for a .1 in header in pcb to allow plugging in the module as well as providing pads to solder the module to the top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
