# Fritzing sketch Rot Enc Shaft (saved by Fritzing 0.9.9b)
breadboards: 1

parts:
  Mod1 = Raspberry Pi Pico
  CUI-enc1 = AMT103
  RE1 = KY-040 Rotary encoder [package=THT]
  R1 = Resistor [tolerance=±5% resistance=10k package="0603 [SMD]"]
  R2 = Resistor [tolerance=±5% resistance=10k package="0603 [SMD]"]

nets:
  GND: Mod1.pin_3, Mod1.pin_8, Mod1.pin_13, Mod1.pin_18, Mod1.pin_23, Mod1.pin_28, Mod1.pin_33, Mod1.pin_38, Mod1.pin_42, CUI-enc1.GND, RE1.GND, R2.Pin_0
  N1: Mod1.pin_15, CUI-enc1.A
  N2: Mod1.pin_16, CUI-enc1.B
  N3: Mod1.pin_17, RE1.CLK
  N4: Mod1.pin_19, RE1.DT
  N5: Mod1.pin_20, RE1.SW
  N6: Mod1.pin_36, RE1.Vcc, R1.Pin_0
  N7: Mod1.pin_40, CUI-enc1.5V

notes:
  3.3 Volts
  5 Volts

custom parts:
  Raspberry Pi Pico: Raspberry Pi Pico. Based around the RP2040 microcontroller the Pico is a low cost microcontroller device bringing Raspberry Pi quality, cost, and easy of use to the microcontroller space. Jan 2021, Split part in to two versions: tht (this one) and SMD. This one will drill holes for a .1 in header in pcb to allow plugging in the module as well as providing pads to solder the module to the top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
  KY-040 Rotary encoder: KY-040 Rotary Encoder with switch on breakout borad from AZ Delivery
