# Fritzing sketch Many_Timers (saved by Fritzing 0.9.9b)
breadboards: 1

parts:
  Mod1 = Raspberry Pi Pico
  LED1 = LED - 3mm [color="Red (633nm)" current=0.030 package="3 mm [THT]"]
  LED2 = LED - 3mm [color="Blue (505nm)" current=0.030 package="3 mm [THT]"]
  LED3 = LED - 3mm [color="Green (565nm)" current=0.030 package="3 mm [THT]"]
  LED4 = LED - 3mm [color="Yellow (585nm)" current=0.030 package="3 mm [THT]"]
  R1 = Resistor [tolerance=±5% resistance=220 package="0402 [SMD]"]
  R2 = Resistor [tolerance=±5% resistance=220 package="0402 [SMD]"]
  R3 = Resistor [tolerance=±5% resistance=220 package="0402 [SMD]"]
  R4 = Resistor [tolerance=±5% resistance=220 package="0402 [SMD]"]

nets:
  N1: Mod1.pin_3, Mod1.pin_8, Mod1.pin_13, Mod1.pin_18, Mod1.pin_23, Mod1.pin_28, Mod1.pin_33, Mod1.pin_38, Mod1.pin_42, R1.Pin_1, R3.Pin_1, R4.Pin_1
  N2: Mod1.pin_16, LED2.anode
  N3: Mod1.pin_17, LED1.anode
  N4: Mod1.pin_19, LED3.anode
  N5: Mod1.pin_20, LED4.anode
  N6: LED1.cathode, R4.Pin_0
  N7: LED2.cathode, R3.Pin_0
  N8: LED3.cathode, R2.Pin_0
  N9: LED4.cathode, R1.Pin_0

custom parts:
  Raspberry Pi Pico: Raspberry Pi Pico. Based around the RP2040 microcontroller the Pico is a low cost microcontroller device bringing Raspberry Pi quality, cost, and easy of use to the microcontroller space. Jan 2021, Split part in to two versions: tht (this one) and SMD. This one will drill holes for a .1 in header in pcb to allow plugging in the module as well as providing pads to solder the module to the top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
