# Fritzing sketch Seven Segment LED (saved by Fritzing 0.9.9b)
breadboards: 1

parts:
  7_Segment1 = 7 Segment Display
  Mod1 = Raspberry Pi Pico
  R2 = Resistor [tolerance=±5% power=0.25 resistance=220 package=THT]
  R3 = Resistor [tolerance=±5% power=0.25 resistance=220 package=THT]
  R4 = Resistor [tolerance=±5% power=0.25 resistance=220 package=THT]
  R5 = Resistor [tolerance=±5% power=0.25 resistance=220 package=THT]
  R6 = Resistor [tolerance=±5% power=0.25 resistance=220 package=THT]
  R7 = Resistor [tolerance=±5% power=0.25 resistance=220 package=THT]
  R8 = Resistor [tolerance=±5% power=0.25 resistance=220 package=THT]
  R9 = Resistor [tolerance=±5% power=0.25 resistance=220 package=THT]

nets:
  N1: 7_Segment1.Segment_G, R9.Pin_1
  N2: 7_Segment1.Segment_F, R8.Pin_1
  N3: 7_Segment1.common_anode, Mod1.pin_3, Mod1.pin_8, Mod1.pin_13, Mod1.pin_18, Mod1.pin_23, Mod1.pin_28, Mod1.pin_33, Mod1.pin_38
  N4: 7_Segment1.Segment_E, R7.Pin_1
  N5: 7_Segment1.Segment_D, R6.Pin_1
  N6: 7_Segment1.Segment_DP, R2.Pin_0
  N7: 7_Segment1.Segment_C, R3.Pin_0
  N8: 7_Segment1.Segment_B, R4.Pin_0
  N9: 7_Segment1.Segment_A, R5.Pin_0
  N10: Mod1.pin_16, R6.Pin_0
  N11: Mod1.pin_17, R7.Pin_0
  N12: Mod1.pin_19, R8.Pin_0
  N13: Mod1.pin_20, R9.Pin_0
  N14: Mod1.pin_21, R5.Pin_1
  N15: Mod1.pin_22, R4.Pin_1
  N16: Mod1.pin_24, R3.Pin_1
  N17: Mod1.pin_25, R2.Pin_1

custom parts:
  Raspberry Pi Pico: Raspberry Pi Pico. Based around the RP2040 microcontroller the Pico is a low cost microcontroller device bringing Raspberry Pi quality, cost, and easy of use to the microcontroller space. Jan 2021, Split part in to two versions: tht (this one) and SMD. This one will drill holes for a .1 in header in pcb to allow plugging in the module as well as providing pads to solder the module to the top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
