# Fritzing sketch Bar Graph LED (saved by Fritzing 0.9.9b)
breadboards: 1

parts:
  D1 = LED_BARGRAPH_10 [package=led_bargaph_10]
  Mod1 = Raspberry Pi Pico
  R1 = Resistor [tolerance=±5% resistance=220 package="2010 [SMD]"]
  R2 = Resistor [tolerance=±5% resistance=220 package="2010 [SMD]"]
  R3 = Resistor [tolerance=±5% resistance=220 package="2010 [SMD]"]
  R4 = Resistor [tolerance=±5% resistance=220 package="2010 [SMD]"]
  R5 = Resistor [tolerance=±5% resistance=220 package="2010 [SMD]"]
  R6 = Resistor [tolerance=±5% resistance=220 package="2010 [SMD]"]
  R7 = Resistor [tolerance=±5% resistance=220 package="2010 [SMD]"]
  R8 = Resistor [tolerance=±5% resistance=220 package="2010 [SMD]"]
  R9 = Resistor [tolerance=±5% resistance=220 package="2010 [SMD]"]
  R10 = Resistor [tolerance=±5% resistance=220 package="2010 [SMD]"]

nets:
  N1: D1.A_A, Mod1.pin_21
  N2: D1.B_A, Mod1.pin_22
  N3: D1.C_A, Mod1.pin_24
  N4: D1.D_A, Mod1.pin_25
  N5: D1.E_A, Mod1.pin_26
  N6: D1.F_A, Mod1.pin_27
  N7: D1.G_A, Mod1.pin_29
  N8: D1.H_A, Mod1.pin_31
  N9: D1.I_A, Mod1.pin_32
  N10: D1.J_A, Mod1.pin_3, Mod1.pin_8, Mod1.pin_13, Mod1.pin_18, Mod1.pin_23, Mod1.pin_28, Mod1.pin_33, Mod1.pin_38, R1.Pin_1, R2.Pin_1, R3.Pin_1, R4.Pin_1, R5.Pin_1, R6.Pin_1, R7.Pin_1, R8.Pin_1, R9.Pin_1, R10.Pin_1
  N11: D1.J_C, R9.Pin_0
  N12: D1.I_C, R8.Pin_0
  N13: D1.H_C, R7.Pin_0
  N14: D1.G_C, R6.Pin_0
  N15: D1.F_C, R5.Pin_0
  N16: D1.E_C, R10.Pin_0
  N17: D1.D_C, R4.Pin_0
  N18: D1.C_C, R3.Pin_0
  N19: D1.B_C, R2.Pin_0
  N20: D1.A_C, R1.Pin_0

custom parts:
  Raspberry Pi Pico: Raspberry Pi Pico. Based around the RP2040 microcontroller the Pico is a low cost microcontroller device bringing Raspberry Pi quality, cost, and easy of use to the microcontroller space. Jan 2021, Split part in to two versions: tht (this one) and SMD. This one will drill holes for a .1 in header in pcb to allow plugging in the module as well as providing pads to solder the module to the top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
