# Fritzing sketch Using Potentiometers (saved by Fritzing 0.9.9b)
breadboards: 1

parts:
  Mod1 = Raspberry Pi Pico
  U1 = POT [package=pot_alpha_rv16af-20]
  U2 = SLIDER [package=slider]
  U3 = POT [package=trim_pot]

nets:
  N1: Mod1.pin_3, Mod1.pin_8, Mod1.pin_13, Mod1.pin_18, Mod1.pin_23, Mod1.pin_28, Mod1.pin_33, Mod1.pin_38, Mod1.pin_42, U1.A, U2.E, U3.S
  N2: Mod1.pin_31, U1.S
  N3: Mod1.pin_32, U2.S
  N4: Mod1.pin_36, U1.E, U2.A, U3.A

notes:
  Rotary 10K
  Linear 30K
  Linear 1K

custom parts:
  Raspberry Pi Pico: Raspberry Pi Pico. Based around the RP2040 microcontroller the Pico is a low cost microcontroller device bringing Raspberry Pi quality, cost, and easy of use to the microcontroller space. Jan 2021, Split part in to two versions: tht (this one) and SMD. This one will drill holes for a .1 in header in pcb to allow plugging in the module as well as providing pads to solder the module to the top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
