# Fritzing sketch RGB LED (saved by Fritzing 0.9.9b)
breadboards: 1

parts:
  Mod1 = Raspberry Pi Pico
  LED1 = RGB LED (com. cathode, rbg) [package="5 mm [THT]"]
  R1 = Resistor [tolerance=±5% resistance=68 package="0603 [SMD]"]
  R2 = Resistor [tolerance=±5% resistance=10 package="0603 [SMD]"]
  R3 = Resistor [tolerance=±5% resistance=10 package="0603 [SMD]"]

nets:
  N1: Mod1.pin_3, Mod1.pin_8, Mod1.pin_13, Mod1.pin_18, Mod1.pin_23, Mod1.pin_28, Mod1.pin_33, Mod1.pin_38, LED1.common_cathode
  N2: Mod1.pin_31, R1.Pin_1
  N3: Mod1.pin_32, R2.Pin_1
  N4: Mod1.pin_34, R3.Pin_1
  N5: LED1.red_anode, R1.Pin_0
  N6: LED1.blue_anode, R2.Pin_0
  N7: LED1.green_anode, R3.Pin_0

custom parts:
  Raspberry Pi Pico: Raspberry Pi Pico. Based around the RP2040 microcontroller the Pico is a low cost microcontroller device bringing Raspberry Pi quality, cost, and easy of use to the microcontroller space. Jan 2021, Split part in to two versions: tht (this one) and SMD. This one will drill holes for a .1 in header in pcb to allow plugging in the module as well as providing pads to solder the module to the top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
