# Fritzing sketch RPR-220 Schematic (saved by Fritzing 0.9.10b)
breadboards: 1

parts:
  Q2 = LTR-301 [package=ltr-301]
  LED1 = smd LED [color="Infrared (880nm)" package="1206 [SMD]"]  # not connected
  Mod1 = Raspberry Pi Pico
  R1 = Resistor [tolerance=±5% resistance=330 package="2010 [SMD]"]
  R2 = Resistor [tolerance=±5% resistance=330 package="2010 [SMD]"]

nets:
  N1: Q2.C, Mod1.pin_3, Mod1.pin_8, Mod1.pin_13, Mod1.pin_18, Mod1.pin_23, Mod1.pin_28, Mod1.pin_33, Mod1.pin_38
  N2: Q2.E, Mod1.pin_20, R2.Pin_0
  N3: Mod1.pin_36, R1.Pin_0, R2.Pin_1

notes:
  IR LED
  IR Photo Transistor
  RPR 220 Reflective Photosensor
  Simulated with discrete components
  Range 39k to 47k ohms
  330 R

custom parts:
  Raspberry Pi Pico: Raspberry Pi Pico. Based around the RP2040 microcontroller the Pico is a low cost microcontroller device bringing Raspberry Pi quality, cost, and easy of use to the microcontroller space. Jan 2021, Split part in to two versions: tht (this one) and SMD. This one will drill holes for a .1 in header in pcb to allow plugging in the module as well as providing pads to solder the module to the top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
