# Fritzing sketch SoundMeter (saved by Fritzing 0.9.10b)
breadboards: 1

parts:
  Mod2 = Raspberry Pi Pico
  D2 = LED_BARGRAPH_10 [package=led_bargaph_10]
  R11 = Resistor [tolerance=±5% resistance=150 package="2010 [SMD]"]
  R12 = Resistor [tolerance=±5% resistance=150 package="2010 [SMD]"]
  R13 = Resistor [tolerance=±5% resistance=150 package="2010 [SMD]"]
  R14 = Resistor [tolerance=±5% resistance=150 package="2010 [SMD]"]
  R15 = Resistor [tolerance=±5% resistance=150 package="2010 [SMD]"]
  R16 = Resistor [tolerance=±5% resistance=150 package="2010 [SMD]"]
  R17 = Resistor [tolerance=±5% resistance=150 package="2010 [SMD]"]
  R18 = Resistor [tolerance=±5% resistance=150 package="2010 [SMD]"]
  R19 = Resistor [tolerance=±5% resistance=150 package="2010 [SMD]"]
  R20 = Resistor [tolerance=±5% resistance=150 package="2010 [SMD]"]
  PART1 = Sound Detector

nets:
  N1: Mod2.pin_3, Mod2.pin_8, Mod2.pin_13, Mod2.pin_18, Mod2.pin_23, Mod2.pin_28, Mod2.pin_33, Mod2.pin_38, R11.Pin_1, R12.Pin_1, R13.Pin_1, R15.Pin_1, R16.Pin_1, R17.Pin_1, R18.Pin_1, R19.Pin_1, PART1.GND
  N2: Mod2.pin_17, D2.J_A
  N3: Mod2.pin_19, D2.I_A
  N4: Mod2.pin_20, D2.H_A
  N5: Mod2.pin_21, D2.A_A
  N6: Mod2.pin_22, D2.B_A
  N7: Mod2.pin_24, D2.C_A
  N8: Mod2.pin_25, D2.D_A
  N9: Mod2.pin_26, D2.E_A
  N10: Mod2.pin_27, D2.F_A
  N11: Mod2.pin_29, D2.G_A
  N12: Mod2.pin_34, PART1.ENVELOPE
  N13: Mod2.pin_36, PART1.VCC
  N14: D2.J_C, R12.Pin_0
  N15: D2.I_C, R13.Pin_0
  N16: D2.H_C, R14.Pin_0
  N17: D2.G_C, R15.Pin_0
  N18: D2.F_C, R16.Pin_0
  N19: D2.E_C, R17.Pin_0
  N20: D2.D_C, R18.Pin_0
  N21: D2.C_C, R19.Pin_0
  N22: D2.B_C, R20.Pin_0
  N23: D2.A_C, R11.Pin_0

custom parts:
  Raspberry Pi Pico: Raspberry Pi Pico. Based around the RP2040 microcontroller the Pico is a low cost microcontroller device bringing Raspberry Pi quality, cost, and easy of use to the microcontroller space. Jan 2021, Split part in to two versions: tht (this one) and SMD. This one will drill holes for a .1 in header in pcb to allow plugging in the module as well as providing pads to solder the module to the top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
  Sound Detector: Electret microphone with multiple outputs. - First output is the actual audio - Second output is the amplitude envelope - Third output is a binary "sound present" indication - high while sound is present, low otherwise. Visit sparkfun.com for more documentations.
