# Fritzing sketch StepperULN2003APG (saved by Fritzing 0.9.10b)
breadboards: 1

parts:
  Mod1 = Raspberry Pi Pico
  Driver2 = 28BYJ-48 Driver Module [part_number=ULN2003 package=THT]
  SM2 = 28BYJ-48 Stepper Motor [part_number=28BYJ-48]
  VCC1 = 4 x AAA Battery Mount

nets:
  N1: Mod1.pin_2, Driver2.IN1
  N2: Mod1.pin_3, Mod1.pin_8, Mod1.pin_13, Mod1.pin_18, Mod1.pin_23, Mod1.pin_28, Mod1.pin_33, Mod1.pin_38
  N3: Mod1.pin_4, Driver2.IN2
  N4: Mod1.pin_5, Driver2.IN3
  N5: Mod1.pin_6, Driver2.IN4
  N6: Driver2.Vmotor, VCC1.+
  N7: Driver2.blue-pin, SM2.blue-pin
  N8: Driver2.pink-pin, SM2.pink-pin
  N9: Driver2.yellow-pin, SM2.yellow-pin
  N10: Driver2.orange-pin, SM2.orange-pin
  N11: Driver2.red-pin, SM2.red-pin

custom parts:
  Raspberry Pi Pico: Raspberry Pi Pico. Based around the RP2040 microcontroller the Pico is a low cost microcontroller device bringing Raspberry Pi quality, cost, and easy of use to the microcontroller space. Jan 2021, Split part in to two versions: tht (this one) and SMD. This one will drill holes for a .1 in header in pcb to allow plugging in the module as well as providing pads to solder the module to the top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
  28BYJ-48 Driver Module: Generic male header
  28BYJ-48 Stepper Motor: Unipolar Stepper Motor 28BYJ-48 Top coil - pink & orange Bottom coil - blue & yellow Common rail - red Connector pins: blue - pink - yellow - orange - red
